# Fritzing sketch HC05_at_mode (saved by Fritzing 0.9.3b)
breadboards: 1

parts:
  Bauteil1 = Bluetooth HC-05 Macho
  R2 = Resistor [tolerance=±5% resistance=1k package="1206 [SMD]"]
  R3 = Resistor [tolerance=±5% resistance=2k package="1206 [SMD]"]
  Bauteil2 = Arduino Uno (Rev3)

nets:
  N1: Bauteil1.TXD, Bauteil2.D10_PWM/SS
  N2: Bauteil1.RXD, R2.Pin_1, R3.Pin_0
  VCC: Bauteil1.VCC, Bauteil2.5V
  N3: Bauteil1.Key, Bauteil2.D9_PWM
  GND: Bauteil1.GND, R3.Pin_1, Bauteil2.GND
  N4: R2.Pin_0, Bauteil2.D11_PWM/MOSI

// code stored in the sketch: at_mode_final.ino
#include <SoftwareSerial.h>

SoftwareSerial BTSerial(10, 11); // RX | TX

void setup()
{
  pinMode(9, OUTPUT);  // this pin will pull the HC-05 pin 34 (key pin) HIGH to switch module to AT mode
  digitalWrite(9, HIGH);
  Serial.begin(9600);
  Serial.println("Enter AT commands:");
  BTSerial.begin(38400);  // HC-05 default speed in AT command more
}

void loop()
{
  // Keep reading from HC-05 and send to Arduino Serial Monitor
  if (BTSerial.available())
    Serial.write(BTSerial.read());

  // Keep reading from Arduino Serial Monitor and send to HC-05
  if (Serial.available())
    BTSerial.write(Serial.read());
}
