# Fritzing sketch HC05_target_scan (saved by Fritzing 0.9.3b)
breadboards: 1

parts:
  Bauteil1 = Bluetooth HC-05 Macho
  R2 = Resistor [tolerance=±5% resistance=1k package="1206 [SMD]"]
  R3 = Resistor [tolerance=±5% resistance=2k package="1206 [SMD]"]
  Bauteil2 = Arduino Uno (Rev3)
  R4 = Resistor [tolerance=±5% resistance=1k package="1206 [SMD]"]
  R5 = Resistor [tolerance=±5% resistance=2k package="1206 [SMD]"]

nets:
  N1: Bauteil1.TXD, Bauteil2.D2
  GND: Bauteil1.RXD, Bauteil1.GND, R2.Pin_1, R3.Pin_0, Bauteil2.GND, R4.Pin_1, R5.Pin_0
  VCC: Bauteil1.VCC, Bauteil2.5V
  N2: R2.Pin_0, Bauteil2.D3_PWM
  N3: Bauteil2.D4, R4.Pin_0

notes:
  pin 34
  touch sensor
  VCC GND SIG
