# Fritzing sketch capacitive_touch_sensor_test (saved by Fritzing 0.9.3b)
breadboards: 1

parts:
  IC1 = IC, DIP package, 6 pins [chip_label="Capacitive Touch Sensor"]
  Bauteil1 = Arduino Nano (Rev3.0)
  LED1 = smd LED [color="Red (633nm)" package="0603 [SMD]"]
  R1 = Resistor [tolerance=±5% resistance=160 package=THT]

nets:
  N1: IC1.pin1, Bauteil1.5V
  N2: IC1.pin2, Bauteil1.GND, LED1.anode
  N3: Bauteil1.D2, R1.Pin_0
  N4: LED1.cathode, R1.Pin_1

// code stored in the sketch: capacitive_touch_sensor_test.ino
#define ctsPin 2
#define ledPin 7

void setup() {
  Serial.begin(9600);
  pinMode(ctsPin, INPUT);
  pinMode(ledPin, OUTPUT);
}

void loop() {
  int ledValue = LOW;
  
  // put your main code here, to run repeatedly:
  int ctsValue = digitalRead(ctsPin);
  
  if (ctsValue == HIGH){
    Serial.println("sensor touched");
    ledValue = HIGH;
  }

  digitalWrite(ledPin, ledValue);
}
