# Fritzing sketch relay_test (saved by Fritzing 0.9.3b)
breadboards: 1

parts:
  Bauteil1 = Arduino Nano (Rev3.0)
  Q1 = NPN-Transistor [package="TO92 [THT]"]
  LED1 = LED - 5mm [color="Red (633nm)" package="5 mm [THT]"]
  R1 = Resistor [tolerance=±5% resistance=220 package=THT]
  VCC1 = 4 x AAA Battery Mount

nets:
  N1: Bauteil1.GND, Q1.E
  N2: Bauteil1.D2, Q1.B
  N3: LED1.cathode, R1.Pin_1
  N4: LED1.anode, VCC1.-

notes:
  same Relay
  NO COM NC
  Relay
  VCC GND SIG
  the relay has a builtin flyback diode
